// Logisim project cpu.circ as structural Verilog: 9 circuits, main circuit HalfAdder
module HalfAdder (
  input  A,
  input  B,
  output S,
  output C
);

  xor xor_1 (S, A, B);
  and and_1 (C, A, B);
endmodule

module FullAdder (
  input  A,
  input  B,
  input  C_in,
  output S,
  output C_out
);

  wire halfadder_1_c, halfadder_1_s, halfadder_2_c;

  HalfAdder halfadder_1 (.A(A), .B(B), .S(halfadder_1_s), .C(halfadder_1_c));
  HalfAdder halfadder_2 (.A(halfadder_1_s), .B(C_in), .S(S), .C(halfadder_2_c));
  or or_1 (C_out, halfadder_1_c, halfadder_2_c);
endmodule

module ALU (
  input  [7:0] A,
  input  [7:0] B,
  input  SUBTRACT,
  output [7:0] S,
  output CF,
  output ZF
);

  wire fulladder_1_c_out, fulladder_2_c_out, fulladder_3_c_out, fulladder_4_c_out, fulladder_5_c_out,
       fulladder_6_c_out, fulladder_7_c_out, xor_1_out, xor_2_out, xor_3_out, xor_4_out, xor_5_out,
       xor_6_out, xor_7_out, xor_8_out;

  xor xor_1 (xor_1_out, B[0], SUBTRACT);
  xor xor_2 (xor_2_out, B[1], SUBTRACT);
  xor xor_3 (xor_3_out, B[2], SUBTRACT);
  xor xor_4 (xor_4_out, B[3], SUBTRACT);
  xor xor_5 (xor_5_out, B[4], SUBTRACT);
  xor xor_6 (xor_6_out, B[5], SUBTRACT);
  xor xor_7 (xor_7_out, B[6], SUBTRACT);
  xor xor_8 (xor_8_out, B[7], SUBTRACT);
  FullAdder fulladder_1 (.A(A[0]), .B(xor_1_out), .C_in(SUBTRACT), .S(S[0]), .C_out(fulladder_1_c_out));
  FullAdder fulladder_2 (.A(A[1]), .B(xor_2_out), .C_in(fulladder_1_c_out), .S(S[1]), .C_out(fulladder_2_c_out));
  FullAdder fulladder_3 (.A(A[2]), .B(xor_3_out), .C_in(fulladder_2_c_out), .S(S[2]), .C_out(fulladder_3_c_out));
  FullAdder fulladder_4 (.A(A[3]), .B(xor_4_out), .C_in(fulladder_3_c_out), .S(S[3]), .C_out(fulladder_4_c_out));
  FullAdder fulladder_5 (.A(A[4]), .B(xor_5_out), .C_in(fulladder_4_c_out), .S(S[4]), .C_out(fulladder_5_c_out));
  FullAdder fulladder_6 (.A(A[5]), .B(xor_6_out), .C_in(fulladder_5_c_out), .S(S[5]), .C_out(fulladder_6_c_out));
  FullAdder fulladder_7 (.A(A[6]), .B(xor_7_out), .C_in(fulladder_6_c_out), .S(S[6]), .C_out(fulladder_7_c_out));
  FullAdder fulladder_8 (.A(A[7]), .B(xor_8_out), .C_in(fulladder_7_c_out), .S(S[7]), .C_out(CF));
  nor nor_1 (ZF, S[0], S[1], S[2], S[3], S[4], S[5], S[6], S[7]);

  // Other names for the same wires on the sheet: SUB = SUBTRACT
endmodule

module MUX8 (
  input  [7:0] D0,
  input  [7:0] D1,
  input  S,
  output [7:0] Q
);

  wire [7:0] and_1_out, and_2_out, bit_extender_1_out;

  assign bit_extender_1_out = {{7{S}}, S};  // Bit_Extender bit_extender_1
  assign and_1_out = D0 & ~bit_extender_1_out;  // AND_Gate and_1, 8 bits wide
  assign and_2_out = bit_extender_1_out & D1;  // AND_Gate and_2, 8 bits wide
  assign Q = and_1_out | and_2_out;  // OR_Gate or_1, 8 bits wide
endmodule

module Counter8 (
  input  ENABLE,
  input  CLK,
  output [7:0] COUNT
);

  wire and_1_out, and_2_out, and_3_out, and_4_out, and_5_out, and_6_out, and_7_out;

  J_K_Flip_Flop j_k_ff_1 (.J(ENABLE), .K(ENABLE), .clk(CLK), .Q(COUNT[0]));  // open: Qn, preset, reset
  and and_1 (and_1_out, ENABLE, COUNT[0]);
  J_K_Flip_Flop j_k_ff_2 (.J(and_1_out), .K(and_1_out), .clk(CLK), .Q(COUNT[1]));  // open: Qn, preset, reset
  and and_2 (and_2_out, and_1_out, COUNT[1]);
  J_K_Flip_Flop j_k_ff_3 (.J(and_2_out), .K(and_2_out), .clk(CLK), .Q(COUNT[2]));  // open: Qn, preset, reset
  and and_3 (and_3_out, and_2_out, COUNT[2]);
  J_K_Flip_Flop j_k_ff_4 (.J(and_3_out), .K(and_3_out), .clk(CLK), .Q(COUNT[3]));  // open: Qn, preset, reset
  and and_4 (and_4_out, and_3_out, COUNT[3]);
  J_K_Flip_Flop j_k_ff_5 (.J(and_4_out), .K(and_4_out), .clk(CLK), .Q(COUNT[4]));  // open: Qn, preset, reset
  and and_5 (and_5_out, and_4_out, COUNT[4]);
  J_K_Flip_Flop j_k_ff_6 (.J(and_5_out), .K(and_5_out), .clk(CLK), .Q(COUNT[5]));  // open: Qn, preset, reset
  and and_6 (and_6_out, and_5_out, COUNT[5]);
  J_K_Flip_Flop j_k_ff_7 (.J(and_6_out), .K(and_6_out), .clk(CLK), .Q(COUNT[6]));  // open: Qn, preset, reset
  and and_7 (and_7_out, and_6_out, COUNT[6]);
  J_K_Flip_Flop j_k_ff_8 (.J(and_7_out), .K(and_7_out), .clk(CLK), .Q(COUNT[7]));  // open: Qn, preset, reset
endmodule

module Register8 (
  input  [7:0] D_in,
  input  CLK,
  output [7:0] D_out
);

  D_Flip_Flop d_ff_1 (.D(D_in[7]), .clk(CLK), .Q(D_out[7]));  // open: Qn, preset, reset
  D_Flip_Flop d_ff_2 (.D(D_in[6]), .clk(CLK), .Q(D_out[6]));  // open: Qn, preset, reset
  D_Flip_Flop d_ff_3 (.D(D_in[5]), .clk(CLK), .Q(D_out[5]));  // open: Qn, preset, reset
  D_Flip_Flop d_ff_4 (.D(D_in[4]), .clk(CLK), .Q(D_out[4]));  // open: Qn, preset, reset
  D_Flip_Flop d_ff_5 (.D(D_in[3]), .clk(CLK), .Q(D_out[3]));  // open: Qn, preset, reset
  D_Flip_Flop d_ff_6 (.D(D_in[2]), .clk(CLK), .Q(D_out[2]));  // open: Qn, preset, reset
  D_Flip_Flop d_ff_7 (.D(D_in[1]), .clk(CLK), .Q(D_out[1]));  // open: Qn, preset, reset
  D_Flip_Flop d_ff_8 (.D(D_in[0]), .clk(CLK), .Q(D_out[0]));  // open: Qn, preset, reset
endmodule

module CPU (
  input  CLK,
  input  [7:0] INSTRUCT,
  output [7:0] A,
  output [7:0] B,
  output [7:0] RES,
  output [7:0] C,
  output [7:0] ADDR
);

  wire and_1_out, and_2_out, d_ff_1_q, d_ff_1_qn, not_1_out, not_2_out, OP0, OP1, OP2, OP3, PC_Load;
  wire [3:0] register_1_q;
  wire [7:0] demultiplexer_1_out0, Dest, RegiPC_d_out, Src;

  not not_1 (not_1_out, CLK);
  and and_1 (and_1_out, and_2_out, not_1_out);
  D_Flip_Flop d_ff_1 (.D(d_ff_1_qn), .clk(and_1_out), .Q(d_ff_1_q), .Qn(d_ff_1_qn));  // open: preset, reset
  Demultiplexer #(.width(8)) demultiplexer_1 (.out0(demultiplexer_1_out0), .out1(Src), .in(INSTRUCT), .sel(d_ff_1_q));
  Register8 RegiA (.D_in(8'h4), .CLK(CLK), .D_out(A));
  Register8 RegiB (.D_in(B), .CLK(CLK), .D_out(B));
  Register8 RegiC (.D_in(C), .CLK(CLK), .D_out(C));
  Register8 RegiPC (.D_in(ADDR), .CLK(CLK), .D_out(RegiPC_d_out));
  not not_2 (not_2_out, d_ff_1_q);
  Register register_1 (
    .D(demultiplexer_1_out0), .en(not_2_out), .clk(CLK), .Q({OP3, OP2, OP1, OP0, register_1_q}));  // open: clr
  Counter PCounter (.load(PC_Load), .up(1'b1), .clk(CLK), .D(RegiPC_d_out), .Q(ADDR));  // open: clr, count, carry
  and and_2 (and_2_out, register_1_q[0], register_1_q[1]);
  ALU alu_1 (.A(Dest), .B(Src), .SUBTRACT(OP1), .S(RES));  // open: CF, ZF
  Multiplexer #(.select(2), .width(8)) multiplexer_1 (
    .in0(A), .in1(B), .in2(C), .out(Src), .sel(register_1_q[1:0]));  // open: in3
  Multiplexer #(.select(2), .width(8)) multiplexer_2 (
    .in0(A), .in1(B), .in2(C), .out(Dest), .sel(register_1_q[3:2]));  // open: in3

  // Other names for the same wires on the sheet: A_D[7:0] = A; B_D[7:0] = B; C_D[7:0] = C; Clock = CLK;
  //   PC_D[7:0] = ADDR
endmodule

module Main (
  output [7:0] out_1,
  output [7:0] out_2,
  output [7:0] out_3
);

  wire clock_1_out;
  wire [7:0] cpu_1_c, rom_1_data;

  ROM rom_1 (.addr(cpu_1_c), .data(rom_1_data));
  Clock clock_1 (.out(clock_1_out));
  CPU cpu_1 (.CLK(clock_1_out), .INSTRUCT(rom_1_data), .A(out_1), .B(out_2), .RES(out_3), .C(cpu_1_c));  // open: ADDR

  // Notes on the sheet:
  //   contents of rom_1 (hex, n*v repeats v):
  //   4a 5a 6a 7a 19
endmodule

module SR_Latch (
  input  R,
  input  S,
  output Q,
  output nQ
);

  nor nor_1 (Q, R, nQ);
  nor nor_2 (nQ, Q, S);
endmodule
